// Logisim project RISCV.circ as structural Verilog: 2 circuits, main circuit main
module main (
);

  wire clock_1_out, risc_vprogramrom_1_p2;
  wire [31:0] inc4_1_s, register_1_q;

  Clock clock_1 (.out(clock_1_out));
  Register #(.width(32)) register_1 (.D(inc4_1_s), .clk(clock_1_out), .Q(register_1_q));  // open: en, clr
  Inc4 inc4_1 (.A(register_1_q), .S(inc4_1_s));
  // RISC_VProgramROM risc_vprogramrom_1: pin names not known; wires that end beside it: register_1_q, risc_vprogramrom_1_p2, risc_vprogramrom_1_p2

  // Notes on the sheet:
  //   contents of risc_vprogramrom_1 (hex, n*v repeats v):
  //   addi t1, x0, 4 add t2, t0, t1
endmodule

module Inc4 (
  input  [31:0] A,
  output [31:0] S
);

  // Incrementer #(.width(30)) incrementer_1: pin names not known; wires that end beside it: A[31:2], S[31:2]

  assign S[1:0] = A[1:0];
endmodule
